// Logisim project CPU_MEM.circ as structural Verilog: 6 circuits, main circuit main
module main (
);

  // CPU_DECODER_3x8 cpu_decoder_3x8_1: pin names not known
endmodule

module CPU_MEM_1 (
  input  S,
  input  E,
  output Q
);

  wire nand_1_out, nand_2_out, nand_4_out;

  nand nand_1 (nand_1_out, S, E);
  nand nand_2 (nand_2_out, nand_1_out, E);
  nand nand_3 (Q, nand_1_out, nand_4_out);
  nand nand_4 (nand_4_out, Q, nand_2_out);

  // Notes on the sheet:
  //   1 bit memory cell
endmodule

module CPU_MEM_8 (
  input  [7:0] in_1,
  input  in_2,
  output [7:0] out_3
);

  CPU_MEM_1 cpu_mem_1_1 (.S(in_1[0]), .E(in_2), .Q(out_3[0]));
  CPU_MEM_1 cpu_mem_1_2 (.S(in_1[1]), .E(in_2), .Q(out_3[1]));
  CPU_MEM_1 cpu_mem_1_3 (.S(in_1[2]), .E(in_2), .Q(out_3[2]));
  CPU_MEM_1 cpu_mem_1_4 (.S(in_1[3]), .E(in_2), .Q(out_3[3]));
  CPU_MEM_1 cpu_mem_1_5 (.S(in_1[4]), .E(in_2), .Q(out_3[4]));
  CPU_MEM_1 cpu_mem_1_6 (.S(in_1[5]), .E(in_2), .Q(out_3[5]));
  CPU_MEM_1 cpu_mem_1_7 (.S(in_1[6]), .E(in_2), .Q(out_3[6]));
  CPU_MEM_1 cpu_mem_1_8 (.S(in_1[7]), .E(in_2), .Q(out_3[7]));
endmodule

module CPU_ENABLE (
  input  [7:0] in_1,
  input  in_2,
  output [7:0] out_3
);

  and and_1 (out_3[0], in_1[0], in_2);
  and and_2 (out_3[1], in_1[1], in_2);
  and and_3 (out_3[2], in_1[2], in_2);
  and and_4 (out_3[3], in_1[3], in_2);
  and and_5 (out_3[4], in_1[4], in_2);
  and and_6 (out_3[5], in_1[5], in_2);
  and and_7 (out_3[6], in_1[6], in_2);
  and and_8 (out_3[7], in_1[7], in_2);
endmodule

module CPU_REG_8 (
  input  [7:0] in_1,
  input  S,
  input  E,
  output [7:0] out_4
);

  wire [7:0] cpu_mem_8_1_out_3;

  CPU_MEM_8 cpu_mem_8_1 (.in_1(in_1), .out_3(cpu_mem_8_1_out_3), .in_2(S));
  CPU_ENABLE cpu_enable_1 (.out_3(out_4), .in_1(cpu_mem_8_1_out_3), .in_2(E));
endmodule

module CPU_DECODER_2X4 (
  input  A,
  input  B,
  output out_3,
  output out_4,
  output out_5,
  output out_6
);

  wire not_1_out, not_2_out;

  not not_1 (not_1_out, A);
  not not_2 (not_2_out, B);
  and _00 (out_3, not_1_out, not_2_out);
  and _01 (out_4, not_1_out, B);
  and _10 (out_5, A, not_2_out);
  and _11 (out_6, A, B);

  // Notes on the sheet:
  //   nA
  //   nB
endmodule
