// Logisim project first_try.circ as structural Verilog: 3 circuits, main circuit main
module main (
  input  in_1,
  input  in_2,
  output out_3,
  output out_4
);

  and and_1 (out_3, in_1, in_2);
  and and_2 (out_4, in_1, 1'b1);

  // Other names for the same wires on the sheet: a = in_1
endmodule

module NAND (
  input  in_1,
  input  in_2,
  output out_3
);

  wire and_1_out;

  and and_1 (and_1_out, in_1, in_2);
  not not_1 (out_3, and_1_out);
endmodule

module C1 (
  input  [7:0] in_1,
  output out_2
);

  wire nand_1_out_3, nand_2_out_3, nand_3_out_3, nand_4_out_3;

  NAND nand_1 (.in_1(in_1[0]), .in_2(in_1[1]), .out_3(nand_1_out_3));
  NAND nand_2 (.in_1(in_1[2]), .in_2(in_1[3]), .out_3(nand_2_out_3));
  NAND nand_3 (.in_1(in_1[4]), .in_2(in_1[5]), .out_3(nand_3_out_3));
  NAND nand_4 (.in_1(in_1[6]), .in_2(in_1[7]), .out_3(nand_4_out_3));
  nor nor_1 (out_2, nand_1_out_3, nand_2_out_3, nand_3_out_3, nand_4_out_3);
endmodule
