// Logisim project play_with_ram.circ as structural Verilog: 1 circuit, main circuit main
module main (
  input  [7:0] in_1,
  input  in_2,
  input  in_3,
  input  in_4,
  input  in_5,
  input  [7:0] in_6,
  output [7:0] out_7
);

  // CPU_RAM_256 cpu_ram_256_1: pin names not known; wires that end beside it: in_3, in_4, in_5, in_6, out_7
endmodule
